# Fritzing sketch radio2 (saved by Fritzing 0.7.0b)
breadboards: 1

parts:
  WeMos_D1_Mini1 = WeMos D1 Mini
  S1 = Pushbutton [package="[THT]"]
  S2 = Pushbutton [package="[THT]"]
  S3 = Pushbutton [package="[THT]"]
  R1 = Resistor [tolerance=±5% resistance=220 package=THT]
  R2 = Resistor [tolerance=±5% resistance=220 package=THT]
  R3 = Resistor [tolerance=±5% resistance=220 package=THT]
  Squix1 = OLED 0.96" 128x64 I2C SSD1306  # not connected
  U1 = MCP1702 Voltage Regulator [package="TO92 [THT]"]
  C1 = Electrolytic Capacitor [capacitance=1µF package="100 mil [THT, electrolytic]"]

nets:
  N1: WeMos_D1_Mini1.3V3, S1.Pin_1, S1.Pin_2, S2.Pin_1, S2.Pin_2, S3.Pin_1, S3.Pin_2, U1.Vout, C1.+
  N2: WeMos_D1_Mini1.D1, S2.Pin_3, S2.Pin_4, R2.Pin_1
  N3: WeMos_D1_Mini1.D2, S3.Pin_3, S3.Pin_4, R1.Pin_1
  N4: WeMos_D1_Mini1.D5, S1.Pin_3, S1.Pin_4, R3.Pin_1
  N5: WeMos_D1_Mini1.G, R1.Pin_0, R2.Pin_0, R3.Pin_0, U1.GND, C1.-

notes:
  Power supply < 30volts
  MCP1702 regulator

custom parts:
  WeMos D1 Mini: The D1 mini is a mini wifi board based on ESP-8266EX.
  MCP1702 Voltage Regulator: A MCP1702 Low Dropout Fixed Voltage Regulator (available in 1.2V, 1.5V, 1.8V, 2.5V, 2.8V, 3.0V, 3.3V, 4.0V, 5.0V)
